# Fritzing sketch Connessioni manuali (saved by Fritzing 0.9.3b)
breadboards: 1

parts:
  Componente1 = Arduino Uno (Rev3)  # not connected
  7_Segment1 = 7 Segment Display
  R1 = Resistor [tolerance=±5% resistance=220 package=THT]  # not connected
  R2 = Resistor [tolerance=±5% resistance=220 package=THT]
  R3 = Resistor [tolerance=±5% resistance=220 package=THT]
  R4 = Resistor [tolerance=±5% resistance=220 package=THT]  # not connected
  R5 = Resistor [tolerance=±5% resistance=220 package=THT]
  R6 = Resistor [tolerance=±5% resistance=220 package=THT]  # not connected
  R7 = Resistor [tolerance=±5% resistance=220 package=THT]
  R8 = Resistor [tolerance=±5% resistance=220 package=THT]  # not connected

nets:
  N1: 7_Segment1.Segment_G, R5.Pin_1
  N2: 7_Segment1.Segment_E, 7_Segment1.Segment_D, R3.Pin_1
  N3: 7_Segment1.Segment_DP, 7_Segment1.Segment_C, R2.Pin_1
  N4: 7_Segment1.Segment_A, R7.Pin_1
