# Fritzing sketch LCD numerici e alfanumerici (saved by Fritzing 0.9.3b)
breadboards: 1

parts:
  Componente1 = Arduino Uno (Rev3)
  R1 = Trimmer Potentiometer [maximum_resistance=10kΩ package=THT]
  LCD1 = LCD screen

nets:
  N1: Componente1.D11_PWM/MOSI, LCD1.DB0
  N2: Componente1.D12/MISO, LCD1.RS
  N3: Componente1.D2, LCD1.DB7
  N4: Componente1.D3_PWM, LCD1.DB6
  N5: Componente1.D4, LCD1.DB5
  N6: Componente1.D5_PWM, LCD1.DB4
  5V: Componente1.5V, R1.leg2, LCD1.VDD, LCD1.LED+
  GND: Componente1.GND, LCD1.VSS, LCD1.E, LCD1.LED-
  N7: R1.wiper, LCD1.V0
